# Fritzing sketch Gundam1Illumination (saved by Fritzing 0.9.3b)
circuit board: 8.46667cm x 5.64444cm
breadboards: 2

parts:
  R1 = Resistor [tolerance=±5% resistance=560 package=THT]
  R2 = Resistor [tolerance=±5% resistance=560 package=THT]
  R3 = Resistor [tolerance=±5% resistance=560 package=THT]
  R4 = Resistor [tolerance=±5% resistance=560 package=THT]
  LED1 = smd LED [color="Red (633nm)" package="0603 [SMD]"]
  LED2 = smd LED [color="Red (633nm)" package="0603 [SMD]"]
  LED5 = smd LED [color="Red (633nm)" package="0603 [SMD]"]
  LED6 = smd LED [color="Red (633nm)" package="0603 [SMD]"]
  VCC1 = Battery block 9V

nets:
  N1: R1.Pin_0, R2.Pin_1, R3.Pin_1, R4.Pin_1, VCC1.-
  N2: R1.Pin_1, LED5.cathode
  N3: R2.Pin_0, LED6.cathode
  N4: R3.Pin_0, LED2.cathode
  N5: R4.Pin_0, LED1.cathode
  N6: LED1.anode, LED2.anode, LED5.anode, LED6.anode, VCC1.+

notes:
  Usare Batteria 9 V, resistenze da 560 oHm
